# Fritzing sketch brewingstation2_updated (saved by Fritzing 1.0.7)
circuit board: 9.26229cm x 5.50598cm
breadboards: 2

parts:
  Level_Shifter = Logic Level Converter
  MAX31865 = Adafruit MAX31865 RTD Sensor Breakout [part_number="Adafruit #3328"]
  Pull_Up_4_7k = Resistor [tolerance=±5% power=0.25 resistance=4.7k package=THT]
  DS18_1 = screw terminal, 3 pins
  DS18_2 = screw terminal, 3 pins
  PExt = Screw terminal - 2 pins [package=THT]
  IDS2 = male pin header, 5 pins [form="♂ (male)"]
  PSwi = Screw terminal - 2 pins [package=THT]
  DOIT_ESP32_DEVKIT_V1 = LuaNode32 / ESP32
  PL0 = screw terminal, 3 pins
  PL1 = screw terminal, 3 pins
  PL2 = screw terminal, 3 pins
  PL3 = screw terminal, 3 pins
  PL4 = screw terminal, 3 pins
  PL5 = screw terminal, 3 pins
  DS18_3 = screw terminal, 3 pins
  GPIO5 = screw terminal, 2 pins
  Relay = screw terminal, 3 pins
  Btn_R1 = Resistor [tolerance=±5% power=0.25 resistance=10k package=THT]
  Btn_R2 = Resistor [tolerance=±5% power=0.25 resistance=10k package=THT]
  Btn_R3 = Resistor [tolerance=±5% power=0.25 resistance=10k package=THT]
  Btn_R4 = Resistor [tolerance=±5% power=0.25 resistance=10k package=THT]
  Btn_R5 = Resistor [tolerance=±5% power=0.25 resistance=10k package=THT]
  GPIO3 = male pin header, 2 pins [form="♂ (male)"]
  Btn_R6 = Resistor [tolerance=±5% power=0.25 resistance=10k package=THT]
  OLED2 = screw terminal, 4 pins
  PJump = Toggle Switch [package=THT]
  PLED = LED - 3mm [color="Red (633nm)" current=0.030 package="3 mm [THT]"]
  OLED1 = screw terminal, 4 pins

nets (from the pcb view):
  N1: Level_Shifter.TX2_LV, DOIT_ESP32_DEVKIT_V1.D18
  N2: Level_Shifter.RX2_LV, DOIT_ESP32_DEVKIT_V1.TX2
  GND: Level_Shifter.GND, MAX31865.GND, DS18_1.pin1, DS18_2.pin1, PExt.pin1, IDS2.pin4, DOIT_ESP32_DEVKIT_V1.GND, PL0.pin1, PL1.pin1, PL2.pin1, PL3.pin1, PL4.pin1, PL5.pin1, DS18_3.pin1, GPIO5.pin1, Relay.pin1, GPIO3.pin1, OLED2.pin1, PLED.cathode, OLED1.pin1
  VIN: Level_Shifter.LV, MAX31865.VIN, Pull_Up_4_7k.Pin_1, DOIT_ESP32_DEVKIT_V1.3V3, Relay.pin2, Btn_R1.Pin_1
  N3: Level_Shifter.RX_LV, DOIT_ESP32_DEVKIT_V1.RX2
  N4: Level_Shifter.TX_LV, DOIT_ESP32_DEVKIT_V1.D15
  N5: Level_Shifter.TX_HV, GPIO5.pin2
  N6: Level_Shifter.RX_HV, IDS2.pin1
  N7: Level_Shifter.HV, IDS2.pin5, PJump.L1
  N8: Level_Shifter.RX2_HV, IDS2.pin3
  N9: Level_Shifter.TX2_HV, IDS2.pin2
  N10: MAX31865.SCLK, DOIT_ESP32_DEVKIT_V1.D23
  N11: MAX31865.SDO, DOIT_ESP32_DEVKIT_V1.TX0
  N12: MAX31865.SDI, DOIT_ESP32_DEVKIT_V1.RX0
  N13: MAX31865.CS, DOIT_ESP32_DEVKIT_V1.D19
  N14: Pull_Up_4_7k.Pin_0, DS18_1.pin2, DS18_2.pin2, DOIT_ESP32_DEVKIT_V1.D4, DS18_3.pin2
  N15: DS18_1.pin3, DS18_2.pin3, PSwi.pin1, DOIT_ESP32_DEVKIT_V1.Vin, DS18_3.pin3, OLED2.pin2, PLED.anode, OLED1.pin2
  N16: PExt.pin2, PJump.L2
  N17: PSwi.pin2, PJump.COM
  N18: DOIT_ESP32_DEVKIT_V1.D34, PL0.pin2, Btn_R1.Pin_0, Btn_R2.Pin_1
  N19: DOIT_ESP32_DEVKIT_V1.D33, Relay.pin3
  N20: DOIT_ESP32_DEVKIT_V1.D25, PL5.pin3
  N21: DOIT_ESP32_DEVKIT_V1.D26, PL4.pin3
  N22: DOIT_ESP32_DEVKIT_V1.D27, PL3.pin3
  N23: DOIT_ESP32_DEVKIT_V1.D14, PL2.pin3
  N24: DOIT_ESP32_DEVKIT_V1.D12, PL1.pin3
  N25: DOIT_ESP32_DEVKIT_V1.D13, PL0.pin3
  N26: DOIT_ESP32_DEVKIT_V1.D5, GPIO3.pin2
  N27: DOIT_ESP32_DEVKIT_V1.D21, OLED2.pin4, OLED1.pin4
  N28: DOIT_ESP32_DEVKIT_V1.D22, OLED2.pin3, OLED1.pin3
  N29: PL1.pin2, Btn_R2.Pin_0, Btn_R3.Pin_1
  N30: PL2.pin2, Btn_R3.Pin_0, Btn_R4.Pin_1
  N31: PL3.pin2, Btn_R4.Pin_0, Btn_R5.Pin_1
  N32: PL4.pin2, Btn_R5.Pin_0, Btn_R6.Pin_1
  N33: PL5.pin2, Btn_R6.Pin_0

notes:
  GND
  5V
  D22
  VIN
  3.3V
  CLK
  SDO
  SDI
  CS
  RDY
  LV
  HV
  brewingstation 2.0
  D16
  D18
  D17
  D33
  3V
  D21
  D4
  D15
  +
  IDS2
  EXT
  _
  D25
  BTN
  D26
  D27
  D14
  D12
  D13
  D5
  TXO
  TXI
  RXI
  RXO
  -
  https://github.com/Gr3yh0und

custom parts:
  Adafruit MAX31865 RTD Sensor Breakout: For precision temperature sensing, nothing beats a Platinum RTD. Resistance temperature detectors (RTDs) are temperature sensors that contain a resistor that changes resistance value as its temperature changes, basically a kind of thermistor. In this sensor, the resistor is actually a small strip of Platinum with a resistance of 100 ohms at 0°C, thus the name PT100. Compared to most NTC/PTC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
  LuaNode32 / ESP32: ESP32 based LuaNode32
