# Fritzing sketch brewingstation (saved by Fritzing 0.9.10b)
circuit board: 8.89519cm x 5.66351cm
breadboards: 1

parts:
  Level_Shifter = Logic Level Converter
  MAX31865 = Adafruit MAX31865 RTD Sensor Breakout [part_number="Adafruit #3328"]
  Pull_Up_4_7k = Resistor [tolerance=±5% power=0.25 resistance=4.7k package=THT]
  DS18B20_1 = screw terminal, 3 pins
  DS18B20_2 = screw terminal, 3 pins
  LED = male pin header, 2 pins [form="♂ (male)"]
  5V_IN = Screw terminal - 2 pins [package=THT]
  IDS2 = male pin header, 5 pins [form="♂ (male)"]
  OLED1 = screw terminal, 4 pins
  J1 = male pin header, 2 pins [form="♂ (male)"]
  Power_Switch = Screw terminal - 2 pins [package=THT]
  BME280 = GY-BMEP280 Barometric Pressure Sensor - Breakout
  GPIO = screw terminal, 11 pins
  Power_OUT = Screw terminal - 2 pins [package=THT]
  NodeMCU_ESP32 = LuaNode32 / ESP32
  OLED2 = screw terminal, 4 pins

nets (from the pcb view):
  N1: Level_Shifter.TX2_LV, NodeMCU_ESP32.D35
  N2: Level_Shifter.RX2_LV, NodeMCU_ESP32.D32
  GND: Level_Shifter.GND, MAX31865.GND, DS18B20_1.pin1, DS18B20_2.pin1, LED.pin1, 5V_IN.pin2, IDS2.pin4, OLED1.pin4, BME280.GND, GPIO.pin1, GPIO.pin6, GPIO.pin10, Power_OUT.pin1, NodeMCU_ESP32.GND, OLED2.pin4
  VIN: Level_Shifter.LV, MAX31865.VIN, Pull_Up_4_7k.Pin_1, BME280.VCC, GPIO.pin11, Power_OUT.pin2, NodeMCU_ESP32.3V3
  N3: Level_Shifter.RX_LV, NodeMCU_ESP32.D21
  N4: Level_Shifter.TX_LV, NodeMCU_ESP32.D18
  N5: Level_Shifter.TX_HV, GPIO.pin2
  N6: Level_Shifter.RX_HV, IDS2.pin3
  N7: Level_Shifter.HV, DS18B20_1.pin3, DS18B20_2.pin3, LED.pin2, Power_Switch.pin1, GPIO.pin5, NodeMCU_ESP32.Vin
  N8: Level_Shifter.RX2_HV, IDS2.pin2
  N9: Level_Shifter.TX2_HV, IDS2.pin1
  N10: MAX31865.SCLK, BME280.SCL, NodeMCU_ESP32.D5
  N11: MAX31865.SDO, BME280.SDO, NodeMCU_ESP32.D19
  N12: MAX31865.SDI, BME280.SDA, NodeMCU_ESP32.D4
  N13: MAX31865.CS, NodeMCU_ESP32.D22
  N14: Pull_Up_4_7k.Pin_0, DS18B20_1.pin2, DS18B20_2.pin2, NodeMCU_ESP32.D34
  N15: 5V_IN.pin1, OLED1.pin3, J1.pin2, Power_Switch.pin2, OLED2.pin3
  N16: IDS2.pin5, J1.pin1
  N17: OLED1.pin1, NodeMCU_ESP32.D15, OLED2.pin1
  N18: OLED1.pin2, NodeMCU_ESP32.D2, OLED2.pin2
  N19: BME280.CSB, NodeMCU_ESP32.D23
  N20: GPIO.pin3, NodeMCU_ESP32.D33
  N21: GPIO.pin4, NodeMCU_ESP32.D25
  N22: GPIO.pin7, NodeMCU_ESP32.D26
  N23: GPIO.pin8, NodeMCU_ESP32.D27
  N24: GPIO.pin9, NodeMCU_ESP32.D14

notes:
  5V
  GND
  D2
  D15
  D27
  VIN
  3.3V
  CLK
  SDO
  SDI
  CS
  RDY
  LV
  HV
  brewing
  1.0
  3V
  D14
  D26
  D25
  D33
  D18
  station
  D21
  D32
  D35
  D34

custom parts:
  Adafruit MAX31865 RTD Sensor Breakout: For precision temperature sensing, nothing beats a Platinum RTD. Resistance temperature detectors (RTDs) are temperature sensors that contain a resistor that changes resistance value as its temperature changes, basically a kind of thermistor. In this sensor, the resistor is actually a small strip of Platinum with a resistance of 100 ohms at 0°C, thus the name PT100. Compared to most NTC/PTC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
  GY-BMEP280 Barometric Pressure Sensor - Breakout: The BME280 is a chip which was originally designed for the next generation of smartphones. It is made up of a very accurate pressure sensor and an associated temperature sensor which helps calibrate the pressure readings. And just for fun they threw in a pretty solid humidity sensor in there as well! So with an I2C connection you have access to enough weather data to make some pretty good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
  LuaNode32 / ESP32: ESP32 based LuaNode32
